# Fritzing sketch 7 segment_breadboard (saved by Fritzing 0.9.2b)
breadboards: 2

parts:
  Explore_AVR_Breakout_Board1 = Explore AVR Breakout Board
  Q1 = NPN-Transistor [package="TO92 [THT]"]
  U1 = 7-SEGMENT-DISPLAY [package=7-segment-display]
  U2 = 7-SEGMENT-DISPLAY [package=7-segment-display]
  U3 = 7-SEGMENT-DISPLAY [package=7-segment-display]
  U4 = 7-SEGMENT-DISPLAY [package=7-segment-display]
  Q2 = NPN-Transistor [package="TO92 [THT]"]
  Q3 = NPN-Transistor [package="TO92 [THT]"]
  Q4 = NPN-Transistor [package="TO92 [THT]"]
  R1 = Resistor [tolerance=±5% resistance=220 package=THT]
  R2 = Resistor [tolerance=±5% resistance=220 package=THT]
  R3 = Resistor [tolerance=±5% resistance=220 package=THT]
  R4 = Resistor [tolerance=±5% resistance=220 package=THT]
  R5 = Resistor [tolerance=±5% resistance=220 package=THT]
  R6 = Resistor [tolerance=±5% resistance=220 package=THT]
  R7 = Resistor [tolerance=±5% resistance=220 package=THT]
  R8 = Resistor [tolerance=±5% resistance=220 package=THT]
  Power_plug1 = Power plug

nets:
  N1: Explore_AVR_Breakout_Board1.PIN3, U1.G2, U2.G2, U3.G2, U4.G2
  N2: Explore_AVR_Breakout_Board1.pin_4, U1.A, U2.A, U3.A, U4.A
  N3: Explore_AVR_Breakout_Board1.pin_5, U1.DP, U2.DP, U3.DP, U4.DP
  N4: Explore_AVR_Breakout_Board1.pin_6, U1.G1
  N5: Explore_AVR_Breakout_Board1.pin_7, U1.D, U2.D, U3.D, U4.D
  N6: Explore_AVR_Breakout_Board1.pin_8, U1.G, U2.G, U3.G, U4.G
  N7: Explore_AVR_Breakout_Board1.pin_9, U1.E, U2.E, U3.E, U4.E
  N8: Explore_AVR_Breakout_Board1.pin_10, U1.B, U2.B, U3.B, U4.B
  N9: Explore_AVR_Breakout_Board1.pin_21, R5.Pin_0
  N10: Explore_AVR_Breakout_Board1.pin_22, R6.Pin_0
  N11: Explore_AVR_Breakout_Board1.pin_23, R7.Pin_0
  N12: Explore_AVR_Breakout_Board1.pin_24, R8.Pin_0
  N13: Explore_AVR_Breakout_Board1.pin_39, Power_plug1.GND
  N14: Explore_AVR_Breakout_Board1.pin_40, R1.Pin_1, R2.Pin_1, R3.Pin_1, R4.Pin_1, Power_plug1.VCC
  N15: Q1.E, R1.Pin_0
  N16: Q1.B, R5.Pin_1
  N17: Q1.C, U1.C, U1.F
  N18: U2.C, U2.F, Q2.C
  N19: U3.C, U3.F, Q3.C
  N20: U4.C, U4.F, Q4.C
  N21: Q2.E, R2.Pin_0
  N22: Q2.B, R6.Pin_1
  N23: Q3.E, R3.Pin_0
  N24: Q3.B, R7.Pin_1
  N25: Q4.E, R4.Pin_0
  N26: Q4.B, R8.Pin_1

notes:
  5V Power Adaptor
