# Fritzing sketch ADC_Light (saved by Fritzing 0.9.2b)

parts:
  Explore_AVR_Breakout_Board1 = Explore AVR Breakout Board  # not connected
  U1 = Explore Ultra One Board [package=THT]

nets:
  N1: U1.pin_107, U1.pin_209
  N2: U1.pin_205, U1.pin_206
