# Fritzing sketch Blink (saved by Fritzing 0.9.2b)

parts:
  U1 = Explore Ultra One Board [package=THT]
  Explore_AVR_Breakout_Board1 = Explore AVR Breakout Board  # not connected

nets:
  N1: U1.pin_76, U1.pin_99
  N2: U1.pin_77, U1.pin_98
  N3: U1.pin_78, U1.pin_97
  N4: U1.pin_79, U1.pin_96
  N5: U1.pin_80, U1.pin_95
  N6: U1.pin_81, U1.pin_94
  N7: U1.pin_82, U1.pin_93
  N8: U1.pin_83, U1.pin_92
