# Fritzing sketch Blink_breadboard (saved by Fritzing 0.9.2b)
breadboards: 2

parts:
  Explore_AVR_Breakout_Board1 = Explore AVR Breakout Board
  LED1 = LED - 5mm [color="Red (633nm)" package="5 mm [THT]"]
  LED2 = LED - 5mm [color="Red (633nm)" package="5 mm [THT]"]
  LED3 = LED - 5mm [color="Red (633nm)" package="5 mm [THT]"]
  LED4 = LED - 5mm [color="Red (633nm)" package="5 mm [THT]"]
  LED5 = LED - 5mm [color="Red (633nm)" package="5 mm [THT]"]
  LED6 = LED - 5mm [color="Red (633nm)" package="5 mm [THT]"]
  LED7 = LED - 5mm [color="Red (633nm)" package="5 mm [THT]"]
  LED8 = LED - 5mm [color="Red (633nm)" package="5 mm [THT]"]
  R1 = Resistor [tolerance=±5% resistance=220 package=THT]
  R2 = Resistor [tolerance=±5% resistance=220 package=THT]
  R3 = Resistor [tolerance=±5% resistance=220 package=THT]
  R4 = Resistor [tolerance=±5% resistance=220 package=THT]
  R5 = Resistor [tolerance=±5% resistance=220 package=THT]
  R6 = Resistor [tolerance=±5% resistance=220 package=THT]
  R7 = Resistor [tolerance=±5% resistance=220 package=THT]
  R8 = Resistor [tolerance=±5% resistance=220 package=THT]
  Power_plug1 = Power plug

nets:
  N1: Explore_AVR_Breakout_Board1.pin_21, R5.Pin_0
  N2: Explore_AVR_Breakout_Board1.pin_22, R7.Pin_0
  N3: Explore_AVR_Breakout_Board1.pin_23, R6.Pin_0
  N4: Explore_AVR_Breakout_Board1.pin_24, R8.Pin_0
  N5: Explore_AVR_Breakout_Board1.pin_25, R4.Pin_0
  N6: Explore_AVR_Breakout_Board1.pin_26, R3.Pin_0
  N7: Explore_AVR_Breakout_Board1.pin_27, R2.Pin_0
  N8: Explore_AVR_Breakout_Board1.pin_28, R1.Pin_0
  N9: Explore_AVR_Breakout_Board1.pin_39, LED1.cathode, LED2.cathode, LED3.cathode, LED4.cathode, LED5.cathode, LED6.cathode, LED7.cathode, LED8.cathode, Power_plug1.GND
  N10: Explore_AVR_Breakout_Board1.pin_40, Power_plug1.VCC
  N11: LED1.anode, R6.Pin_1
  N12: LED2.anode, R8.Pin_1
  N13: LED3.anode, R4.Pin_1
  N14: LED4.anode, R3.Pin_1
  N15: LED5.anode, R2.Pin_1
  N16: LED6.anode, R1.Pin_1
  N17: LED7.anode, R7.Pin_1
  N18: LED8.anode, R5.Pin_1

notes:
  5V Adaptor
  Limiting Resistors = 1k
