# Fritzing sketch Buzzer (saved by Fritzing 0.9.2b)

parts:
  U1 = Explore Ultra One Board [package=THT]
  Explore_AVR_Breakout_Board1 = Explore AVR Breakout Board  # not connected

nets:
  N1: U1.pin_88, U1.pin_154
