# Fritzing sketch Buzzer_breadboard (saved by Fritzing 0.9.2b)
breadboards: 2

parts:
  Explore_AVR_Breakout_Board1 = Explore AVR Breakout Board
  Q1 = NPN-Transistor [package="TO92 [THT]"]
  J1 = Piezo Speaker
  R1 = Resistor [tolerance=±5% resistance=220 package=THT]
  Power_plug1 = Power plug

nets:
  N1: Explore_AVR_Breakout_Board1.PIN3, R1.Pin_0
  N2: Explore_AVR_Breakout_Board1.pin_39, J1.pin1, Power_plug1.GND
  N3: Explore_AVR_Breakout_Board1.pin_40, Q1.E, Power_plug1.VCC
  N4: Q1.B, R1.Pin_1
  N5: Q1.C, J1.pin2

notes:
  5V Adapter
