# Fritzing sketch DC MOTOR (saved by Fritzing 0.9.2b)

parts:
  Explore_AVR_Breakout_Board1 = Explore AVR Breakout Board  # not connected
  U1 = Explore Ultra One Board [package=THT]
  M1 = DC Motor  # not connected
  M2 = DC Motor  # not connected

nets:
  N1: U1.pin_64, U1.pin_167
  N2: U1.pin_65, U1.pin_168
  N3: U1.pin_66, U1.pin_169
  N4: U1.pin_67, U1.pin_171
