# Fritzing sketch Keypad (saved by Fritzing 0.9.2b)

parts:
  Explore_AVR_Breakout_Board1 = Explore AVR Breakout Board  # not connected
  U1 = Explore Ultra One Board [package=THT]
  LCD1 = LCD screen  # not connected

nets:
  N1: U1.pin_96, U1.pin_198
  N2: U1.pin_97, U1.pin_199
  N3: U1.pin_98, U1.pin_200
  N4: U1.pin_99, U1.pin_201
  N5: U1.pin_154, U1.pin_175
  N6: U1.pin_155, U1.pin_174
  N7: U1.pin_156, U1.pin_173
  N8: U1.pin_157, U1.pin_172
  N9: U1.pin_158, U1.pin_179
  N10: U1.pin_159, U1.pin_178
  N11: U1.pin_160, U1.pin_177
  N12: U1.pin_161, U1.pin_176
  N13: U1.pin_169, U1.pin_189
  N14: U1.pin_170, U1.pin_190
  N15: U1.pin_171, U1.pin_191
