# Fritzing sketch LCD (saved by Fritzing 0.9.2b)

parts:
  Explore_AVR_Breakout_Board1 = Explore AVR Breakout Board  # not connected
  U1 = Explore Ultra One Board [package=THT]
  LCD1 = LCD screen  # not connected

nets:
  N1: U1.pin_154, U1.pin_189
  N2: U1.pin_155, U1.pin_190
  N3: U1.pin_156, U1.pin_191
  N4: U1.pin_168, U1.pin_198
  N5: U1.pin_169, U1.pin_199
  N6: U1.pin_170, U1.pin_200
  N7: U1.pin_171, U1.pin_201
