# Fritzing sketch LCD8bitmode (saved by Fritzing 0.9.2b)

parts:
  Explore_AVR_Breakout_Board1 = Explore AVR Breakout Board  # not connected
  LCD1 = LCD screen  # not connected
  U1 = Explore Ultra One Board [package=THT]

nets:
  N1: U1.pin_93, U1.pin_195
  N2: U1.pin_94, U1.pin_196
  N3: U1.pin_95, U1.pin_197
  N4: U1.pin_107, U1.pin_191
  N5: U1.pin_108, U1.pin_190
  N6: U1.pin_109, U1.pin_189
  N7: U1.pin_154, U1.pin_194
  N8: U1.pin_158, U1.pin_198
  N9: U1.pin_159, U1.pin_199
  N10: U1.pin_160, U1.pin_200
  N11: U1.pin_161, U1.pin_201
