# Fritzing sketch OLED (saved by Fritzing 0.9.2b)

parts:
  Explore_AVR_Breakout_Board1 = Explore AVR Breakout Board  # not connected
  U1 = Explore Ultra One Board [package=THT]
  OLED1 = 128x32 SPI I2C OLEDDisplay  # not connected

nets:
  N1: U1.pin_92, U1.pin_183
  N2: U1.pin_93, U1.pin_182

custom parts:
  128x32 SPI I2C OLEDDisplay: 128x32 SPI OLED Monochrome Display
