# Fritzing sketch RTC_UART (saved by Fritzing 0.9.2b)

parts:
  Explore_AVR_Breakout_Board1 = Explore AVR Breakout Board  # not connected
  U1 = Explore Ultra One Board [package=THT]

nets:
  N1: U1.pin_89, U1.pin_93
  N2: U1.pin_90, U1.pin_92
