# Fritzing sketch Switch (saved by Fritzing 0.9.2b)

parts:
  U1 = Explore Ultra One Board [package=THT]
  Explore_AVR_Breakout_Board1 = Explore AVR Breakout Board  # not connected

nets:
  N1: U1.pin_68, U1.pin_109
  N2: U1.pin_69, U1.pin_108
  N3: U1.pin_70, U1.pin_107
  N4: U1.pin_71, U1.pin_106
  N5: U1.pin_72, U1.pin_105
  N6: U1.pin_73, U1.pin_104
  N7: U1.pin_74, U1.pin_103
  N8: U1.pin_75, U1.pin_102
  N9: U1.pin_76, U1.pin_99
  N10: U1.pin_77, U1.pin_98
  N11: U1.pin_78, U1.pin_97
  N12: U1.pin_79, U1.pin_96
  N13: U1.pin_80, U1.pin_95
  N14: U1.pin_81, U1.pin_94
  N15: U1.pin_82, U1.pin_93
  N16: U1.pin_83, U1.pin_92
