# Fritzing sketch Cascaded Matrx LED breakout with Arduino (saved by Fritzing 0.9.2b)

parts:
  8x8_LED_matrix_MAX1 = 8x8 Red 8x8 LED Matrix with MAX7219
  Part1 = Arduino Uno (Rev3)
  8x8_LED_matrix_MAX2 = 8x8 Red 8x8 LED Matrix with MAX7219

nets:
  VCC: 8x8_LED_matrix_MAX1.VCC, 8x8_LED_matrix_MAX1.VCC_PT, Part1.5V, 8x8_LED_matrix_MAX2.VCC, 8x8_LED_matrix_MAX2.VCC_PT
  GND: 8x8_LED_matrix_MAX1.GND, 8x8_LED_matrix_MAX1.CLK_PT, Part1.GND, 8x8_LED_matrix_MAX2.GND_PT, 8x8_LED_matrix_MAX2.CLK
  N1: 8x8_LED_matrix_MAX1.GND_PT, 8x8_LED_matrix_MAX1.CLK, Part1.D11_PWM/MOSI, 8x8_LED_matrix_MAX2.GND, 8x8_LED_matrix_MAX2.CLK_PT
  N2: 8x8_LED_matrix_MAX1.DIN, Part1.D12/MISO
  N3: 8x8_LED_matrix_MAX1.DIN_CHN, 8x8_LED_matrix_MAX1.CS, Part1.D10_PWM/SS, 8x8_LED_matrix_MAX2.DIN
  N4: 8x8_LED_matrix_MAX1.CS_PT, 8x8_LED_matrix_MAX2.DIN_CHN, 8x8_LED_matrix_MAX2.CS

custom parts:
  8x8 Red 8x8 LED Matrix with MAX7219: Description: 8 by 8 red LED matrix with a MAX7219 controller.
