# Fritzing sketch Joystick with Arduino (saved by Fritzing 0.9.2b)

parts:
  Part1 = Arduino Uno (Rev3)
  Part3 = Thumb Joystick

nets:
  N1: Part1.A0, Part3.VRx
  N2: Part1.A1, Part3.VRy
  N3: Part1.D2, Part3.SW
  5V: Part1.5V, Part3.+5V
  GND: Part1.GND, Part3.GND
