# Fritzing sketch Matrx LED and Joystick with Arduino (saved by Fritzing 0.9.2b)
breadboards: 1

parts:
  8x8_LED_matrix_MAX1 = 8x8 Red 8x8 LED Matrix with MAX7219
  Part1 = Arduino Uno (Rev3)
  Part2 = Thumb Joystick

nets:
  VCC: 8x8_LED_matrix_MAX1.VCC, 8x8_LED_matrix_MAX1.VCC_PT, Part1.5V, Part2.+5V
  GND: 8x8_LED_matrix_MAX1.GND, 8x8_LED_matrix_MAX1.CLK_PT, Part1.GND, Part2.GND
  N1: 8x8_LED_matrix_MAX1.GND_PT, 8x8_LED_matrix_MAX1.CLK, Part1.D11_PWM/MOSI
  N2: 8x8_LED_matrix_MAX1.DIN, Part1.D12/MISO
  N3: 8x8_LED_matrix_MAX1.DIN_CHN, 8x8_LED_matrix_MAX1.CS, Part1.D10_PWM/SS
  N4: Part1.A0, Part2.VRx
  N5: Part1.A1, Part2.VRy
  N6: Part1.D2, Part2.SW

custom parts:
  8x8 Red 8x8 LED Matrix with MAX7219: Description: 8 by 8 red LED matrix with a MAX7219 controller.
