# Fritzing sketch OLED with 8051 (saved by Fritzing 0.9.2b)

parts:
  Part1 = Explore Starter 8051
  OLED_I2C1 = OLED 128x64 I2C Monochrome Display

nets:
  N1: Part1.P0.0, OLED_I2C1.SCK
  N2: Part1.P0.1, OLED_I2C1.SDA
  GND: Part1.GND, OLED_I2C1.GND
  +5V: Part1.+5V, OLED_I2C1.VDD
