# Fritzing sketch Rotory encoder with nokia lcd (saved by Fritzing 0.9.2b)
breadboards: 1

parts:
  Nokia_5110_LCD_Module1 = Nokia 5110 LCD basado en PCD8544
  ENCODER1 = Rotary Encoder
  Part1 = Arduino Uno (Rev3)
  R1 = Resistor [tolerance=±5% resistance=220 package=THT]
  R2 = Resistor [tolerance=±5% resistance=220 package=THT]
  R3 = Resistor [tolerance=±5% resistance=220 package=THT]
  R4 = Resistor [tolerance=±5% resistance=220 package=THT]
  R5 = Resistor [tolerance=±5% resistance=220 package=THT]
  R6 = Resistor [tolerance=±5% resistance=220 package=THT]

nets:
  VCC: Nokia_5110_LCD_Module1.VCC, ENCODER1.VCC, Part1.3V3, R6.Pin_0
  GND: Nokia_5110_LCD_Module1.GND, ENCODER1.GND, Part1.GND
  N1: Nokia_5110_LCD_Module1.CE, R2.Pin_1
  N2: Nokia_5110_LCD_Module1.RST, R1.Pin_1
  N3: Nokia_5110_LCD_Module1.DC, R3.Pin_1
  N4: Nokia_5110_LCD_Module1.DIN, R4.Pin_1
  N5: Nokia_5110_LCD_Module1.CLK, R5.Pin_1
  N6: Nokia_5110_LCD_Module1.LIGHT, R6.Pin_1
  N7: ENCODER1.SW, Part1.D9_PWM
  N8: ENCODER1.GT, Part1.D2
  N9: ENCODER1.CLK, Part1.D3_PWM
  N10: Part1.D8, R1.Pin_0
  N11: Part1.D4, R2.Pin_0
  N12: Part1.D5_PWM, R3.Pin_0
  N13: Part1.D6_PWM, R4.Pin_0
  N14: Part1.D7, R5.Pin_0

custom parts:
  Nokia 5110 LCD basado en PCD8544: Módulo Nokia 5110 LCD basado en el controlador PCD8544. Versión de 8 pines (sólo entrada).
